# Fritzing sketch Amiga 500 Joystick (saved by Fritzing 0.9.3b)
breadboards: 1

parts:
  S1 = Pushbutton [package="[THT]"]
  S2 = Pushbutton [package="[THT]"]
  S3 = Pushbutton [package="[THT]"]
  S4 = Pushbutton [package="[THT]"]
  S5 = Pushbutton [package="[THT]"]
  Componente1 = Arduino Uno (Rev3)
  X1 = DB9 Connector [package=db9]

nets:
  N1: S1.Pin_1, S1.Pin_2, Componente1.D1/TX
  N2: S1.Pin_3, S1.Pin_4, S2.Pin_1, S2.Pin_2, S3.Pin_3, S3.Pin_4, S4.Pin_3, S4.Pin_4, S5.Pin_3, S5.Pin_4, Componente1.GND, X1.8
  N3: S2.Pin_3, S2.Pin_4, Componente1.D2
  N4: S3.Pin_1, S3.Pin_2, Componente1.D4
  N5: S4.Pin_1, S4.Pin_2, Componente1.D3_PWM
  N6: S5.Pin_1, S5.Pin_2, Componente1.D5_PWM
  N7: Componente1.D8, X1.1
  N8: Componente1.D9_PWM, X1.2
  N9: Componente1.D10_PWM/SS, X1.3
  N10: Componente1.D11_PWM/MOSI, X1.4
  N11: Componente1.D12/MISO, X1.6
  N12: Componente1.VIN, X1.7

// code stored in the sketch: Untitled2.ino
/**
 * In input (dai pushbuttons)
 * pin 1 - forward
 * pin 2 - backward
 * pin 3 - left
 * pin 4 - right
 * pin 5 - fire
 * 
 * In output (da Arduino al connettore DB9)
 * pin 8 - forward
 * pin 9 - backward
 * pin 10 - left
 * pin 11 - right
 * pin 12 - fire
 */

const int forwardIn = 1;
const int backwardIn = 2;
const int leftIn = 3;
const int rightIn = 4;
const int fireIn = 5;

const int forwardOut = 8;
const int backwardOut = 9;
const int leftOut = 10;
const int rightOut = 11;
const int fireOut = 12;

void setup() {
  // put your setup code here, to run once:
  pinMode(forwardIn, INPUT_PULLUP);
  pinMode(backwardIn, INPUT_PULLUP);
  pinMode(leftIn, INPUT_PULLUP);
  pinMode(rightIn, INPUT_PULLUP);
  pinMode(fireIn, INPUT_PULLUP);

  pinMode(forwardOut, OUTPUT);
  pinMode(backwardOut, OUTPUT);
  pinMode(leftOut, OUTPUT);
  pinMode(rightOut, OUTPUT);
  pinMode(fireOut, OUTPUT);

  digitalWrite(forwardOut, HIGH);
  digitalWrite(backwardOut, HIGH);
  digitalWrite(leftOut, HIGH);
  digitalWrite(rightOut, HIGH);
  digitalWrite(fireOut, HIGH);
}

/*
 * Nell'interfaccia JOYSTICK di Amiga una funzione ? attivata da un segnale basso.
 */
void loop() {
  // Forward
  digitalWrite(forwardOut, digitalRead(forwardIn));

  // Backward
  digitalWrite(backwardOut, digitalRead(backwardIn));

  // Left
  digitalWrite(leftOut, digitalRead(leftIn));

  // Right
  digitalWrite(rightOut, digitalRead(rightIn));

  // Fire
  digitalWrite(fireOut, digitalRead(fireIn));
}
